# Fritzing sketch Flower_Pot_Midterm_AM (saved by Fritzing 1.0.4)
breadboards: 3

parts:
  Breadboard4 = Breadboard Split Power
  Breadboard5 = Breadboard Split Power
  A2 = photon2
  Chirp!_Soil_Moisture_Sensor1 = Chirp! Soil Moisture Sensor v2.7.3
  WATER_PUMP1 = water pump/motor  # not connected
  Water_Level_Sensor1 = Water Level Sensor  # not connected
  SENS1 = SoilWatch 10  # not connected
  Grove1 = Grove Dust Sensor  # not connected
  OLED_I2C1 = OLED 128x64 I2C Monochrome Display
  Part1 = MQ-131 breakout

nets:
  GND: Breadboard4.pin3Z, Breadboard4.pin29Z, Breadboard5.pin3Z, Breadboard5.pin29Z, OLED_I2C1.GND, Part1.GND
  N1: Breadboard4.pin4Y, Breadboard4.pin15Y, Breadboard4.pin17Y, Breadboard4.pin29Y, Breadboard5.pin3Y, Breadboard5.pin15Y, Breadboard5.pin17Y, Breadboard5.pin29Y, OLED_I2C1.VDD
  N2: A2.Pin_3, Part1.DO
  N3: A2.Pin_4, A2.Pin_30, A2.Pin_35, Chirp!_Soil_Moisture_Sensor1.pin_5
  N4: A2.Pin_6, Chirp!_Soil_Moisture_Sensor1.pin_3
  N5: A2.Pin_17, OLED_I2C1.SDA
  N6: A2.Pin_18, OLED_I2C1.SCK
  N7: A2.Pin_28, A2.Pin_29

custom parts:
  Breadboard Split Power: A custom 6 pin per group power supply strip where the top row (ground) is all bussed together and the bottom row (+V) is split in two groups of 12 pins. This version is modified to be a loadable part and was rescaled to be on the standard 1px = 1thou grid with the size set in inches
  photon2: The Photon 2 is a development module with a microcontroller and Wi-Fi networking.
  water pump/motor: WATER PUMP BY ARDUBLOCKTR
  Water Level Sensor: A water level sensor. This sensor operates at 3V to 5V. The Sig (signal) pin outputs an analogue signal that is in proportion to the amount of water in contact with the sensor.
  SoilWatch 10: SoilWatch 10 - Capacitive soil moisture sensor
  Grove Dust Sensor: PPD42 Grove Dust Sensor
  MQ-131 breakout: SKU: 101282
